# Fritzing sketch arduspeedo (saved by Fritzing 0.9.2b)

parts:
  Part1 = Arduino Uno (Rev3) - ICSP
  BAT1 = BC9VPC [package=bc9vpc]  # not connected
  LED1 = 7-SEGMENT-4DIGIT-YOUNGSUN [package=7-segment-4digit-youngsun-longpads]

nets:
  N1: Part1.GND, LED1.DIG3
  N2: Part1.D4, LED1.E
  N3: Part1.D5_PWM, LED1.COL-A
  N4: Part1.3V3, LED1.DP
